// Logisim project SEGA 315-5309.circ as structural Verilog: 2 circuits, main circuit main
module main (
  input  VCLK,
  input  nSRES,
  input  TEST,
  input  ZA0,
  input  ZA1,
  input  ZA2,
  input  ZA3,
  input  ZA4,
  input  ZA5,
  input  ZA6,
  input  ZA7,
  input  A0,
  input  A1,
  input  A2,
  input  A3,
  input  A4,
  input  A5,
  input  A6,
  input  A7,
  input  D0,
  input  D1,
  input  D2,
  input  D3,
  input  D4,
  input  D5,
  input  D6,
  input  D7,
  input  D8,
  input  D9,
  input  D10,
  input  D11,
  input  D12,
  input  D13,
  input  D14,
  input  D15,
  input  ZD0,
  input  ZD1,
  input  ZD2,
  input  ZD3,
  input  ZD4,
  input  ZD5,
  input  ZD6,
  input  ZD7,
  input  EM31,
  input  EM32,
  input  EM33,
  input  EM34,
  input  EM36,
  input  EM38,
  input  EM37,
  input  EM11,
  input  EM12,
  input  EM13,
  input  EM14,
  input  EM16,
  input  EM18,
  input  EM17,
  input  EM21,
  input  EM22,
  input  EM23,
  input  EM24,
  input  EM26,
  input  EM28,
  input  EM27,
  input  nVTOZ,
  input  nZTOV,
  input  nIO,
  input  nM3,
  input  FREQ,
  input  LANG,
  input  nCAS0,
  input  nLWR,
  input  nDISK,
  input  nFRES,
  output D0_2,
  output D1_2,
  output D2_2,
  output D3_2,
  output D4_2,
  output D5_2,
  output D6_2,
  output D7_2,
  output D8_2,
  output D9_2,
  output D10_2,
  output D11_2,
  output D12_2,
  output D13_2,
  output D14_2,
  output D15_2,
  output ZD0_2,
  output ZD1_2,
  output ZD2_2,
  output ZD3_2,
  output ZD4_2,
  output ZD5_2,
  output ZD6_2,
  output ZD7_2,
  output EM31_2,
  output EM32_2,
  output EM33_2,
  output EM34_2,
  output EM36_2,
  output EM38_2,
  output EM37_2,
  output EM11_2,
  output EM12_2,
  output EM13_2,
  output EM14_2,
  output EM16_2,
  output EM18_2,
  output EM17_2,
  output EM21_2,
  output EM22_2,
  output EM23_2,
  output EM24_2,
  output EM26_2,
  output EM28_2,
  output EM27_2,
  output nHL
);

  wire _78_nq, _79_out, _80_co, _80_nq, _81_co, _81_nq, _81_q, _129_co, _129_nq, _130_co, _130_nq, _132_out,
       _133_co, _133_nq, _134_nq, _188_co, _188_nq, _238_q, _239_q, _240_q, _242_out, _243_q, _244_q, _345_q,
       _346_q, _347_q, _349_out, _642_out, _643_out, _644_out, _645_out, multiplexer_1_out,
       multiplexer_3_out, nFRES_t, undriven;
  wire [1:0] undriven_2;

  buf _642 (_642_out, _79_out);  // AND_Gate
  and _645 (_645_out, _132_out, undriven);
  nor _643 (_643_out, nFRES_t, _642_out);
  and _242 (_242_out, _645_out, _644_out);
  buf _644 (_644_out, _643_out);
  D_Flip_Flop _595 (.clk(VCLK), .D(nSRES));  // open: Q, Qn, preset, en, reset
  _1_bit_cnt _129 (.C(VCLK), .nLD(_644_out), .nQ(_129_nq), .CO(_129_co));  // open: CIN, VAL, nRES, Q
  _1_bit_cnt _130 (.C(VCLK), .CIN(_129_co), .nLD(_644_out), .nQ(_130_nq), .CO(_130_co));  // open: VAL, nRES, Q
  _1_bit_cnt _133 (.CIN(_130_co), .nLD(_644_out), .nQ(_133_nq), .CO(_133_co));  // open: C, VAL, nRES, Q
  _1_bit_cnt _134 (.CIN(_133_co), .nLD(_644_out), .nQ(_134_nq));  // open: C, VAL, nRES, Q, CO
  _1_bit_cnt _188 (.C(VCLK), .CIN(_242_out), .nLD(_644_out), .nQ(_188_nq), .CO(_188_co));  // open: VAL, nRES, Q
  _1_bit_cnt _80 (.C(VCLK), .CIN(_188_co), .nLD(_644_out), .nQ(_80_nq), .CO(_80_co));  // open: VAL, nRES, Q
  _1_bit_cnt _81 (.C(VCLK), .CIN(_80_co), .nLD(_644_out), .Q(_81_q), .nQ(_81_nq), .CO(_81_co));  // open: VAL, nRES
  _1_bit_cnt _78 (.C(VCLK), .CIN(_81_co), .nLD(_644_out), .nQ(_78_nq));  // open: VAL, nRES, Q, CO
  nor _132 (_132_out, _134_nq, _133_nq, _130_nq, _129_nq);
  nor _79 (_79_out, _78_nq, _81_nq, _80_nq, _188_nq);
  Multiplexer #(.disabled(0), .enable("false")) multiplexer_1 (
    .in0(_81_q), .out(multiplexer_1_out), .sel(TEST));  // open: in1
  T_Flip_Flop _239 (.clk(multiplexer_1_out), .Q(_239_q));  // open: T, Qn, preset, reset, en
  T_Flip_Flop _240 (.clk(_239_q), .Q(_240_q));  // open: T, Qn, preset, reset, en
  T_Flip_Flop _244 (.clk(_240_q), .Q(_244_q));  // open: T, Qn, preset, reset, en
  T_Flip_Flop _243 (.clk(_244_q), .Q(_243_q));  // open: T, Qn, preset, reset, en
  T_Flip_Flop _238 (.clk(_243_q), .Q(_238_q));  // open: T, Qn, preset, reset, en
  T_Flip_Flop _347 (.clk(_238_q), .Q(_347_q));  // open: T, Qn, preset, reset, en
  T_Flip_Flop _346 (.clk(_347_q), .Q(_346_q));  // open: T, Qn, preset, reset, en
  T_Flip_Flop _345 (.clk(_346_q), .Q(_345_q));  // open: T, Qn, preset, reset, en
  Multiplexer #(.select(2), .disabled(0), .enable("false")) multiplexer_2 (
    .in0(multiplexer_1_out), .in1(_240_q), .in2(_239_q), .in3(_243_q), .sel(undriven_2));  // open: out
  Multiplexer #(.select(2), .disabled(0), .enable("false")) multiplexer_3 (
    .in0(_243_q), .in1(_347_q), .in2(_238_q), .in3(_345_q), .out(multiplexer_3_out), .sel(undriven_2));
  not _349 (_349_out, multiplexer_3_out);

  // Notes on the sheet:
  //   248
  //   295
  //   295
  //   A
  //   SEGA 315-5309
endmodule

// COUNTER 1BIT
module _1_bit_cnt (
  input  C,
  input  CIN,
  input  VAL,
  input  nLD,
  input  nRES,
  output Q,
  output nQ,
  output CO
);

  wire d_ff_1_q, multiplexer_1_out, not_1_out, not_2_out, xor_1_out;

  not not_1 (not_1_out, nRES);
  xor xor_1 (xor_1_out, Q, CIN);
  and and_1 (CO, Q, CIN);
  Multiplexer #(.disabled(0), .enable("false")) multiplexer_1 (
    .in0(VAL), .in1(xor_1_out), .out(multiplexer_1_out), .sel(nLD));
  not not_2 (not_2_out, C);
  D_Flip_Flop #(.trigger("high")) d_ff_1 (
    .clk(C), .D(multiplexer_1_out), .Q(d_ff_1_q), .reset(not_1_out));  // open: Qn, preset, en
  D_Flip_Flop #(.trigger("high")) d_ff_2 (
    .clk(not_2_out), .D(d_ff_1_q), .Q(Q), .Qn(nQ), .reset(not_1_out));  // open: preset, en

  // Notes on the sheet:
  //   C
  //   VAL
  //   LD
  //   /RES
  //   CIN
  //   CNT BIT
  //   Q
  //   nQ
  //   CO
endmodule
